# Fritzing sketch 10x10-rgd-led-matrix (saved by Fritzing 0.9.3b)
circuit board: 12cm x 11cm
breadboards: 1

parts:
  Q1 = PNP-Transistor [part_number=2N4402 package="TO92 [THT]"]
  Q2 = PNP-Transistor [part_number=2N4402 package="TO92 [THT]"]
  Q3 = PNP-Transistor [part_number=2N4402 package="TO92 [THT]"]
  Q4 = PNP-Transistor [part_number=2N4402 package="TO92 [THT]"]
  Q5 = PNP-Transistor [part_number=2N4402 package="TO92 [THT]"]
  Q6 = PNP-Transistor [part_number=2N4402 package="TO92 [THT]"]
  Q7 = PNP-Transistor [part_number=2N4402 package="TO92 [THT]"]
  Q8 = PNP-Transistor [part_number=2N4402 package="TO92 [THT]"]
  R1 = Resistor [tolerance=±5% resistance=1k package=THT]
  R2 = Resistor [tolerance=±5% resistance=1k package=THT]
  R3 = Resistor [tolerance=±5% resistance=1k package=THT]
  R4 = Resistor [tolerance=±5% resistance=1k package=THT]
  R5 = Resistor [tolerance=±5% resistance=1k package=THT]
  R6 = Resistor [tolerance=±5% resistance=1k package=THT]
  R7 = Resistor [tolerance=±5% resistance=1k package=THT]
  R8 = Resistor [tolerance=±5% resistance=1k package=THT]
  R11 = Resistor [tolerance=±5% resistance=150 package=THT]
  R12 = Resistor [tolerance=±5% resistance=100 package=THT]
  R13 = Resistor [tolerance=±5% resistance=100 package=THT]
  R14 = Resistor [tolerance=±5% resistance=150 package=THT]
  R15 = Resistor [tolerance=±5% resistance=100 package=THT]
  R16 = Resistor [tolerance=±5% resistance=100 package=THT]
  R17 = Resistor [tolerance=±5% resistance=150 package=THT]
  R18 = Resistor [tolerance=±5% resistance=100 package=THT]
  R19 = Resistor [tolerance=±5% resistance=100 package=THT]
  R20 = Resistor [tolerance=±5% resistance=150 package=THT]
  R21 = Resistor [tolerance=±5% resistance=100 package=THT]
  R22 = Resistor [tolerance=±5% resistance=100 package=THT]
  R23 = Resistor [tolerance=±5% resistance=150 package=THT]
  R24 = Resistor [tolerance=±5% resistance=100 package=THT]
  R25 = Resistor [tolerance=±5% resistance=100 package=THT]
  R26 = Resistor [tolerance=±5% resistance=150 package=THT]
  R27 = Resistor [tolerance=±5% resistance=100 package=THT]
  R28 = Resistor [tolerance=±5% resistance=100 package=THT]
  R29 = Resistor [tolerance=±5% resistance=150 package=THT]
  R30 = Resistor [tolerance=±5% resistance=100 package=THT]
  R31 = Resistor [tolerance=±5% resistance=100 package=THT]
  R32 = Resistor [tolerance=±5% resistance=150 package=THT]
  R33 = Resistor [tolerance=±5% resistance=100 package=THT]
  R34 = Resistor [tolerance=±5% resistance=100 package=THT]
  U3 = 74HC595 [package="DIP16 [THT]"]
  U5 = 74HC595 [package="DIP16 [THT]"]
  C1 = Ceramic Capacitor [capacitance=100nF package="100 mil [THT, multilayer]"]
  C2 = Ceramic Capacitor [capacitance=100nF package="100 mil [THT, multilayer]"]
  C3 = Ceramic Capacitor [capacitance=100nF package="100 mil [THT, multilayer]"]
  C5 = Ceramic Capacitor [capacitance=100nF package="100 mil [THT, multilayer]"]
  U1 = 74HC595 [package="DIP16 [THT]"]
  D1 = Schottky Diode [part_number=BAT43 package="300 mil [THT]"]
  D2 = Schottky Diode [part_number=BAT43 package="300 mil [THT]"]
  D3 = Schottky Diode [part_number=BAT43 package="300 mil [THT]"]
  D4 = Schottky Diode [part_number=BAT43 package="300 mil [THT]"]
  D5 = Schottky Diode [part_number=BAT43 package="300 mil [THT]"]
  D6 = Schottky Diode [part_number=BAT43 package="300 mil [THT]"]
  D7 = Schottky Diode [part_number=BAT43 package="300 mil [THT]"]
  D8 = Schottky Diode [part_number=BAT43 package="300 mil [THT]"]
  U2 = 74HC595 [package="DIP16 [THT]"]
  R41 = Resistor [tolerance=±5% resistance=1k package=THT]
  R42 = Resistor [tolerance=±5% resistance=1k package=THT]
  R43 = Resistor [tolerance=±5% resistance=1k package=THT]
  R44 = Resistor [tolerance=±5% resistance=1k package=THT]
  R45 = Resistor [tolerance=±5% resistance=1k package=THT]
  R46 = Resistor [tolerance=±5% resistance=1k package=THT]
  R47 = Resistor [tolerance=±5% resistance=1k package=THT]
  R48 = Resistor [tolerance=±5% resistance=1k package=THT]
  R40 = Resistor [tolerance=±5% resistance=100 package=THT]
  R39 = Resistor [tolerance=±5% resistance=100 package=THT]
  R38 = Resistor [tolerance=±5% resistance=150 package=THT]
  R37 = Resistor [tolerance=±5% resistance=100 package=THT]
  R36 = Resistor [tolerance=±5% resistance=100 package=THT]
  R35 = Resistor [tolerance=±5% resistance=150 package=THT]
  R50 = Resistor [tolerance=±5% resistance=1k package=THT]
  R49 = Resistor [tolerance=±5% resistance=1k package=THT]
  D10 = Schottky Diode [part_number=BAT43 package="300 mil [THT]"]
  D9 = Schottky Diode [part_number=BAT43 package="300 mil [THT]"]
  R10 = Resistor [tolerance=±5% resistance=1k package=THT]
  R9 = Resistor [tolerance=±5% resistance=1k package=THT]
  Q10 = PNP-Transistor [part_number=2N4402 package="TO92 [THT]"]
  Q9 = PNP-Transistor [part_number=2N4402 package="TO92 [THT]"]
  C4 = Ceramic Capacitor [capacitance=100nF package="100 mil [THT, multilayer]"]
  LED1 = RGB LED - (4 legs) [package="5 mm [THT]"]
  LED0 = RGB LED - (4 legs) [package="5 mm [THT]"]
  LED2 = RGB LED - (4 legs) [package="5 mm [THT]"]
  LED3 = RGB LED - (4 legs) [package="5 mm [THT]"]
  LED4 = RGB LED - (4 legs) [package="5 mm [THT]"]
  LED5 = RGB LED - (4 legs) [package="5 mm [THT]"]
  LED6 = RGB LED - (4 legs) [package="5 mm [THT]"]
  LED7 = RGB LED - (4 legs) [package="5 mm [THT]"]
  LED8 = RGB LED - (4 legs) [package="5 mm [THT]"]
  LED9 = RGB LED - (4 legs) [package="5 mm [THT]"]
  LED10 = RGB LED - (4 legs) [package="5 mm [THT]"]
  LED11 = RGB LED - (4 legs) [package="5 mm [THT]"]
  LED12 = RGB LED - (4 legs) [package="5 mm [THT]"]
  LED13 = RGB LED - (4 legs) [package="5 mm [THT]"]
  LED14 = RGB LED - (4 legs) [package="5 mm [THT]"]
  LED15 = RGB LED - (4 legs) [package="5 mm [THT]"]
  LED16 = RGB LED - (4 legs) [package="5 mm [THT]"]
  LED17 = RGB LED - (4 legs) [package="5 mm [THT]"]
  LED18 = RGB LED - (4 legs) [package="5 mm [THT]"]
  LED19 = RGB LED - (4 legs) [package="5 mm [THT]"]
  LED20 = RGB LED - (4 legs) [package="5 mm [THT]"]
  LED21 = RGB LED - (4 legs) [package="5 mm [THT]"]
  LED22 = RGB LED - (4 legs) [package="5 mm [THT]"]
  LED23 = RGB LED - (4 legs) [package="5 mm [THT]"]
  LED24 = RGB LED - (4 legs) [package="5 mm [THT]"]
  LED25 = RGB LED - (4 legs) [package="5 mm [THT]"]
  LED26 = RGB LED - (4 legs) [package="5 mm [THT]"]
  LED27 = RGB LED - (4 legs) [package="5 mm [THT]"]
  LED28 = RGB LED - (4 legs) [package="5 mm [THT]"]
  LED29 = RGB LED - (4 legs) [package="5 mm [THT]"]
  LED30 = RGB LED - (4 legs) [package="5 mm [THT]"]
  LED31 = RGB LED - (4 legs) [package="5 mm [THT]"]
  LED32 = RGB LED - (4 legs) [package="5 mm [THT]"]
  LED33 = RGB LED - (4 legs) [package="5 mm [THT]"]
  LED34 = RGB LED - (4 legs) [package="5 mm [THT]"]
  LED35 = RGB LED - (4 legs) [package="5 mm [THT]"]
  LED36 = RGB LED - (4 legs) [package="5 mm [THT]"]
  LED37 = RGB LED - (4 legs) [package="5 mm [THT]"]
  LED36_2 = RGB LED - (4 legs) [package="5 mm [THT]"]
  LED39 = RGB LED - (4 legs) [package="5 mm [THT]"]
  LED40 = RGB LED - (4 legs) [package="5 mm [THT]"]
  LED41 = RGB LED - (4 legs) [package="5 mm [THT]"]
  LED42 = RGB LED - (4 legs) [package="5 mm [THT]"]
  LED43 = RGB LED - (4 legs) [package="5 mm [THT]"]
  LED44 = RGB LED - (4 legs) [package="5 mm [THT]"]
  LED45 = RGB LED - (4 legs) [package="5 mm [THT]"]
  LED46 = RGB LED - (4 legs) [package="5 mm [THT]"]
  LED48 = RGB LED - (4 legs) [package="5 mm [THT]"]
  LED71 = RGB LED - (4 legs) [package="5 mm [THT]"]
  LED49 = RGB LED - (4 legs) [package="5 mm [THT]"]
  LED50 = RGB LED - (4 legs) [package="5 mm [THT]"]
  LED51 = RGB LED - (4 legs) [package="5 mm [THT]"]
  LED52 = RGB LED - (4 legs) [package="5 mm [THT]"]
  LED53 = RGB LED - (4 legs) [package="5 mm [THT]"]
  LED54 = RGB LED - (4 legs) [package="5 mm [THT]"]
  LED55 = RGB LED - (4 legs) [package="5 mm [THT]"]
  LED56 = RGB LED - (4 legs) [package="5 mm [THT]"]
  LED57 = RGB LED - (4 legs) [package="5 mm [THT]"]
  LED58 = RGB LED - (4 legs) [package="5 mm [THT]"]
  LED59 = RGB LED - (4 legs) [package="5 mm [THT]"]
  LED60 = RGB LED - (4 legs) [package="5 mm [THT]"]
  LED61 = RGB LED - (4 legs) [package="5 mm [THT]"]
  LED62 = RGB LED - (4 legs) [package="5 mm [THT]"]
  LED63 = RGB LED - (4 legs) [package="5 mm [THT]"]
  LED64 = RGB LED - (4 legs) [package="5 mm [THT]"]
  LED65 = RGB LED - (4 legs) [package="5 mm [THT]"]
  LED66 = RGB LED - (4 legs) [package="5 mm [THT]"]
  LED67 = RGB LED - (4 legs) [package="5 mm [THT]"]
  LED68 = RGB LED - (4 legs) [package="5 mm [THT]"]
  LED69 = RGB LED - (4 legs) [package="5 mm [THT]"]
  LED70 = RGB LED - (4 legs) [package="5 mm [THT]"]
  LED71_2 = RGB LED - (4 legs) [package="5 mm [THT]"]
  LED72 = RGB LED - (4 legs) [package="5 mm [THT]"]
  LED73 = RGB LED - (4 legs) [package="5 mm [THT]"]
  LED74 = RGB LED - (4 legs) [package="5 mm [THT]"]
  LED75 = RGB LED - (4 legs) [package="5 mm [THT]"]
  LED76 = RGB LED - (4 legs) [package="5 mm [THT]"]
  LED77 = RGB LED - (4 legs) [package="5 mm [THT]"]
  LED78 = RGB LED - (4 legs) [package="5 mm [THT]"]
  LED79 = RGB LED - (4 legs) [package="5 mm [THT]"]
  LED80 = RGB LED - (4 legs) [package="5 mm [THT]"]
  LED81 = RGB LED - (4 legs) [package="5 mm [THT]"]
  LED82 = RGB LED - (4 legs) [package="5 mm [THT]"]
  LED83 = RGB LED - (4 legs) [package="5 mm [THT]"]
  LED84 = RGB LED - (4 legs) [package="5 mm [THT]"]
  LED85 = RGB LED - (4 legs) [package="5 mm [THT]"]
  LED86 = RGB LED - (4 legs) [package="5 mm [THT]"]
  LED87 = RGB LED - (4 legs) [package="5 mm [THT]"]
  LED88 = RGB LED - (4 legs) [package="5 mm [THT]"]
  LED89 = RGB LED - (4 legs) [package="5 mm [THT]"]
  LED90 = RGB LED - (4 legs) [package="5 mm [THT]"]
  LED91 = RGB LED - (4 legs) [package="5 mm [THT]"]
  LED92 = RGB LED - (4 legs) [package="5 mm [THT]"]
  LED93 = RGB LED - (4 legs) [package="5 mm [THT]"]
  LED94 = RGB LED - (4 legs) [package="5 mm [THT]"]
  LED95 = RGB LED - (4 legs) [package="5 mm [THT]"]
  LED96 = RGB LED - (4 legs) [package="5 mm [THT]"]
  LED97 = RGB LED - (4 legs) [package="5 mm [THT]"]
  LED98 = RGB LED - (4 legs) [package="5 mm [THT]"]
  LED99 = RGB LED - (4 legs) [package="5 mm [THT]"]
  J2 = male pin header, 5 pins [form="♂ (male)"]
  U4 = 74HC595 [package="DIP16 [THT]"]
  J1 = male pin header, 5 pins [form="♂ (male)"]

nets:
  5V: Q1.E, Q2.E, Q3.E, Q4.E, Q5.E, Q6.E, Q7.E, Q8.E, U3.MR, U3.VCC, U5.MR, U5.VCC, C1.1, C2.1, C3.1, C5.1, U1.MR, U1.VCC, U2.MR, U2.VCC, Q10.E, Q9.E, C4.1, J2.pin1, U4.MR, U4.VCC, J1.pin1
  N1: Q1.B, R1.Pin_0, D1.cathode
  N2: Q1.C, D1.anode, R41.Pin_1, LED1.common_anode, LED0.common_anode, LED2.common_anode, LED3.common_anode, LED4.common_anode, LED5.common_anode, LED6.common_anode, LED7.common_anode, LED8.common_anode, LED9.common_anode
  N3: Q2.B, R2.Pin_0, D2.cathode
  N4: Q2.C, D2.anode, R42.Pin_1, LED10.common_anode, LED11.common_anode, LED12.common_anode, LED13.common_anode, LED14.common_anode, LED15.common_anode, LED16.common_anode, LED17.common_anode, LED18.common_anode, LED19.common_anode
  N5: Q3.B, R3.Pin_0, D3.cathode
  N6: Q3.C, D3.anode, R43.Pin_1, LED20.common_anode, LED21.common_anode, LED22.common_anode, LED23.common_anode, LED24.common_anode, LED25.common_anode, LED26.common_anode, LED27.common_anode, LED28.common_anode, LED29.common_anode
  N7: Q4.B, R4.Pin_0, D4.cathode
  N8: Q4.C, D4.anode, R44.Pin_1, LED30.common_anode, LED31.common_anode, LED32.common_anode, LED33.common_anode, LED34.common_anode, LED35.common_anode, LED36.common_anode, LED37.common_anode, LED36_2.common_anode, LED39.common_anode
  N9: Q5.B, R5.Pin_0, D5.cathode
  N10: Q5.C, D5.anode, R45.Pin_1, LED40.common_anode, LED41.common_anode, LED42.common_anode, LED43.common_anode, LED44.common_anode, LED45.common_anode, LED46.common_anode, LED48.common_anode, LED71.common_anode, LED49.common_anode
  N11: Q6.B, R6.Pin_0, D6.cathode
  N12: Q6.C, D6.anode, R46.Pin_1, LED50.common_anode, LED51.common_anode, LED52.common_anode, LED53.common_anode, LED54.common_anode, LED55.common_anode, LED56.common_anode, LED57.common_anode, LED58.common_anode, LED59.common_anode
  N13: Q7.B, R7.Pin_0, D7.cathode
  N14: Q7.C, D7.anode, R47.Pin_1, LED60.common_anode, LED61.common_anode, LED62.common_anode, LED63.common_anode, LED64.common_anode, LED65.common_anode, LED66.common_anode, LED67.common_anode, LED68.common_anode, LED69.common_anode
  N15: Q8.B, R8.Pin_0, D8.cathode
  N16: Q8.C, D8.anode, R48.Pin_1, LED70.common_anode, LED71_2.common_anode, LED72.common_anode, LED73.common_anode, LED74.common_anode, LED75.common_anode, LED76.common_anode, LED77.common_anode, LED78.common_anode, LED79.common_anode
  N17: R1.Pin_1, U5.Q0
  N18: R2.Pin_1, U5.Q1
  N19: R3.Pin_1, U5.Q2
  N20: R4.Pin_1, U5.Q3
  N21: R5.Pin_1, U5.Q4
  N22: R6.Pin_1, U5.Q5
  N23: R7.Pin_1, U5.Q6
  N24: R8.Pin_1, U5.Q7
  N25: R11.Pin_0, U1.Q7
  N26: R11.Pin_1, LED0.red_cathode, LED10.red_cathode, LED20.red_cathode, LED30.red_cathode, LED40.red_cathode, LED50.red_cathode, LED60.red_cathode, LED70.red_cathode, LED80.red_cathode, LED90.red_cathode
  N27: R12.Pin_0, U1.Q6
  N28: R12.Pin_1, LED0.green_cathode, LED10.green_cathode, LED20.green_cathode, LED30.green_cathode, LED40.green_cathode, LED50.green_cathode, LED60.green_cathode, LED70.green_cathode, LED80.green_cathode, LED90.green_cathode
  N29: R13.Pin_0, U1.Q5
  N30: R13.Pin_1, LED0.blue_cathode, LED10.blue_cathode, LED20.blue_cathode, LED30.blue_cathode, LED40.blue_cathode, LED50.blue_cathode, LED60.blue_cathode, LED70.blue_cathode, LED80.blue_cathode, LED90.blue_cathode
  N31: R14.Pin_0, U1.Q4
  N32: R14.Pin_1, LED1.red_cathode, LED11.red_cathode, LED21.red_cathode, LED31.red_cathode, LED41.red_cathode, LED51.red_cathode, LED61.red_cathode, LED71_2.red_cathode, LED81.red_cathode, LED91.red_cathode
  N33: R15.Pin_0, U1.Q3
  N34: R15.Pin_1, LED1.green_cathode, LED11.green_cathode, LED21.green_cathode, LED31.green_cathode, LED41.green_cathode, LED51.green_cathode, LED61.green_cathode, LED71_2.green_cathode, LED81.green_cathode, LED91.green_cathode
  N35: R16.Pin_0, U1.Q2
  N36: R16.Pin_1, LED1.blue_cathode, LED11.blue_cathode, LED21.blue_cathode, LED31.blue_cathode, LED41.blue_cathode, LED51.blue_cathode, LED61.blue_cathode, LED71_2.blue_cathode, LED81.blue_cathode, LED91.blue_cathode
  N37: R17.Pin_0, U1.Q1
  N38: R17.Pin_1, LED2.red_cathode, LED12.red_cathode, LED22.red_cathode, LED32.red_cathode, LED42.red_cathode, LED52.red_cathode, LED62.red_cathode, LED72.red_cathode, LED82.red_cathode, LED92.red_cathode
  N39: R18.Pin_0, U1.Q0
  N40: R18.Pin_1, LED2.green_cathode, LED12.green_cathode, LED22.green_cathode, LED32.green_cathode, LED42.green_cathode, LED52.green_cathode, LED62.green_cathode, LED72.green_cathode, LED82.green_cathode, LED92.green_cathode
  N41: R19.Pin_0, U2.Q7
  N42: R19.Pin_1, LED2.blue_cathode, LED12.blue_cathode, LED22.blue_cathode, LED32.blue_cathode, LED42.blue_cathode, LED52.blue_cathode, LED62.blue_cathode, LED72.blue_cathode, LED82.blue_cathode, LED92.blue_cathode
  N43: R20.Pin_0, U2.Q6
  N44: R20.Pin_1, LED3.red_cathode, LED13.red_cathode, LED23.red_cathode, LED33.red_cathode, LED43.red_cathode, LED53.red_cathode, LED63.red_cathode, LED73.red_cathode, LED83.red_cathode, LED93.red_cathode
  N45: R21.Pin_0, U2.Q5
  N46: R21.Pin_1, LED3.green_cathode, LED13.green_cathode, LED23.green_cathode, LED33.green_cathode, LED43.green_cathode, LED53.green_cathode, LED63.green_cathode, LED73.green_cathode, LED83.green_cathode, LED93.green_cathode
  N47: R22.Pin_0, U2.Q4
  N48: R22.Pin_1, LED3.blue_cathode, LED13.blue_cathode, LED23.blue_cathode, LED33.blue_cathode, LED43.blue_cathode, LED53.blue_cathode, LED63.blue_cathode, LED73.blue_cathode, LED83.blue_cathode, LED93.blue_cathode
  N49: R23.Pin_0, U2.Q3
  N50: R23.Pin_1, LED4.red_cathode, LED14.red_cathode, LED24.red_cathode, LED34.red_cathode, LED44.red_cathode, LED54.red_cathode, LED64.red_cathode, LED74.red_cathode, LED84.red_cathode, LED94.red_cathode
  N51: R24.Pin_0, U2.Q2
  N52: R24.Pin_1, LED4.green_cathode, LED14.green_cathode, LED24.green_cathode, LED34.green_cathode, LED44.green_cathode, LED54.green_cathode, LED64.green_cathode, LED74.green_cathode, LED84.green_cathode, LED94.green_cathode
  N53: R25.Pin_0, U2.Q1
  N54: R25.Pin_1, LED4.blue_cathode, LED14.blue_cathode, LED24.blue_cathode, LED34.blue_cathode, LED44.blue_cathode, LED54.blue_cathode, LED64.blue_cathode, LED74.blue_cathode, LED84.blue_cathode, LED94.blue_cathode
  N55: R26.Pin_0, U2.Q0
  N56: R26.Pin_1, LED5.red_cathode, LED15.red_cathode, LED25.red_cathode, LED35.red_cathode, LED45.red_cathode, LED55.red_cathode, LED65.red_cathode, LED75.red_cathode, LED85.red_cathode, LED95.red_cathode
  N57: R27.Pin_0, U3.Q7
  N58: R27.Pin_1, LED5.green_cathode, LED15.green_cathode, LED25.green_cathode, LED35.green_cathode, LED45.green_cathode, LED55.green_cathode, LED65.green_cathode, LED75.green_cathode, LED85.green_cathode, LED95.green_cathode
  N59: R28.Pin_0, U3.Q6
  N60: R28.Pin_1, LED5.blue_cathode, LED15.blue_cathode, LED25.blue_cathode, LED35.blue_cathode, LED45.blue_cathode, LED55.blue_cathode, LED65.blue_cathode, LED75.blue_cathode, LED85.blue_cathode, LED95.blue_cathode
  N61: R29.Pin_0, U3.Q5
  N62: R29.Pin_1, LED6.red_cathode, LED16.red_cathode, LED26.red_cathode, LED36.red_cathode, LED46.red_cathode, LED56.red_cathode, LED66.red_cathode, LED76.red_cathode, LED86.red_cathode, LED96.red_cathode
  N63: R30.Pin_0, U3.Q4
  N64: R30.Pin_1, LED6.green_cathode, LED16.green_cathode, LED26.green_cathode, LED36.green_cathode, LED46.green_cathode, LED56.green_cathode, LED66.green_cathode, LED76.green_cathode, LED86.green_cathode, LED96.green_cathode
  N65: R31.Pin_0, U3.Q3
  N66: R31.Pin_1, LED6.blue_cathode, LED16.blue_cathode, LED26.blue_cathode, LED36.blue_cathode, LED46.blue_cathode, LED56.blue_cathode, LED66.blue_cathode, LED76.blue_cathode, LED86.blue_cathode, LED96.blue_cathode
  N67: R32.Pin_0, U3.Q2
  N68: R32.Pin_1, LED7.red_cathode, LED17.red_cathode, LED27.red_cathode, LED37.red_cathode, LED48.red_cathode, LED57.red_cathode, LED67.red_cathode, LED77.red_cathode, LED87.red_cathode, LED97.red_cathode
  N69: R33.Pin_0, U3.Q1
  N70: R33.Pin_1, LED7.green_cathode, LED17.green_cathode, LED27.green_cathode, LED37.green_cathode, LED48.green_cathode, LED57.green_cathode, LED67.green_cathode, LED77.green_cathode, LED87.green_cathode, LED97.green_cathode
  N71: R34.Pin_0, U3.Q0
  N72: R34.Pin_1, LED7.blue_cathode, LED17.blue_cathode, LED27.blue_cathode, LED37.blue_cathode, LED48.blue_cathode, LED57.blue_cathode, LED67.blue_cathode, LED77.blue_cathode, LED87.blue_cathode, LED97.blue_cathode
  GND: U3.GND, U3.OE, U5.GND, U5.OE, C1.0, C2.0, C3.0, C5.0, U1.GND, U1.OE, U2.GND, U2.OE, R41.Pin_0, R42.Pin_0, R43.Pin_0, R44.Pin_0, R45.Pin_0, R46.Pin_0, R47.Pin_0, R48.Pin_0, R50.Pin_0, R49.Pin_0, C4.0, J2.pin2, U4.GND, U4.OE, J1.pin2
  N73: U3.Q7', U2.DS
  N74: U3.SH_CP, U5.SH_CP, U1.SH_CP, U2.SH_CP, J2.pin4, U4.SH_CP, J1.pin4
  N75: U3.ST_CP, U5.ST_CP, U1.ST_CP, U2.ST_CP, J2.pin5, U4.ST_CP, J1.pin5
  N76: U3.DS, U4.Q7'
  N77: U5.Q7', U4.DS
  N78: U5.DS, J1.pin3
  N79: U1.Q7', J2.pin3
  N80: U1.DS, U2.Q7'
  N81: R40.Pin_0, U4.Q2
  N82: R40.Pin_1, LED9.blue_cathode, LED19.blue_cathode, LED29.blue_cathode, LED39.blue_cathode, LED49.blue_cathode, LED59.blue_cathode, LED69.blue_cathode, LED79.blue_cathode, LED89.blue_cathode, LED99.blue_cathode
  N83: R39.Pin_0, U4.Q3
  N84: R39.Pin_1, LED9.green_cathode, LED19.green_cathode, LED29.green_cathode, LED39.green_cathode, LED49.green_cathode, LED59.green_cathode, LED69.green_cathode, LED79.green_cathode, LED89.green_cathode, LED99.green_cathode
  N85: R38.Pin_0, U4.Q4
  N86: R38.Pin_1, LED9.red_cathode, LED19.red_cathode, LED29.red_cathode, LED39.red_cathode, LED49.red_cathode, LED59.red_cathode, LED69.red_cathode, LED79.red_cathode, LED89.red_cathode, LED99.red_cathode
  N87: R37.Pin_0, U4.Q5
  N88: R37.Pin_1, LED8.blue_cathode, LED18.blue_cathode, LED28.blue_cathode, LED36_2.blue_cathode, LED71.blue_cathode, LED58.blue_cathode, LED68.blue_cathode, LED78.blue_cathode, LED88.blue_cathode, LED98.blue_cathode
  N89: R36.Pin_0, U4.Q6
  N90: R36.Pin_1, LED8.green_cathode, LED18.green_cathode, LED28.green_cathode, LED36_2.green_cathode, LED71.green_cathode, LED58.green_cathode, LED68.green_cathode, LED78.green_cathode, LED88.green_cathode, LED98.green_cathode
  N91: R35.Pin_0, U4.Q7
  N92: R35.Pin_1, LED8.red_cathode, LED18.red_cathode, LED28.red_cathode, LED36_2.red_cathode, LED71.red_cathode, LED58.red_cathode, LED68.red_cathode, LED78.red_cathode, LED88.red_cathode, LED98.red_cathode
  N93: R50.Pin_1, D10.anode, Q10.C, LED90.common_anode, LED91.common_anode, LED92.common_anode, LED93.common_anode, LED94.common_anode, LED95.common_anode, LED96.common_anode, LED97.common_anode, LED98.common_anode, LED99.common_anode
  N94: R49.Pin_1, D9.anode, Q9.C, LED80.common_anode, LED81.common_anode, LED82.common_anode, LED83.common_anode, LED84.common_anode, LED85.common_anode, LED86.common_anode, LED87.common_anode, LED88.common_anode, LED89.common_anode
  N95: D10.cathode, R10.Pin_0, Q10.B
  N96: D9.cathode, R9.Pin_0, Q9.B
  N97: R10.Pin_1, U4.Q1
  N98: R9.Pin_1, U4.Q0

notes:
  LATCH
  CLK
  SER
  GND
  +5V
  SER'
  10x10 RGB LED Matrix
  www.kamprath.net/led-matrix
  (c) 2017 Michael Kamprath
  v1.0
  IN
  OUT
