# Fritzing sketch 4x4-rgd-led-matrix (saved by Fritzing 0.9.3b)
circuit board: 7cm x 7.5cm
breadboards: 2

parts:
  LED1 = RGB LED (com. anode, rbg) [package="5 mm [THT]"]
  LED2 = RGB LED (com. anode, rbg) [package="5 mm [THT]"]
  LED3 = RGB LED (com. anode, rbg) [package="5 mm [THT]"]
  LED4 = RGB LED (com. anode, rbg) [package="5 mm [THT]"]
  LED5 = RGB LED (com. anode, rbg) [package="5 mm [THT]"]
  LED6 = RGB LED (com. anode, rbg) [package="5 mm [THT]"]
  LED7 = RGB LED (com. anode, rbg) [package="5 mm [THT]"]
  LED8 = RGB LED (com. anode, rbg) [package="5 mm [THT]"]
  LED9 = RGB LED (com. anode, rbg) [package="5 mm [THT]"]
  LED10 = RGB LED (com. anode, rbg) [package="5 mm [THT]"]
  LED11 = RGB LED (com. anode, rbg) [package="5 mm [THT]"]
  LED12 = RGB LED (com. anode, rbg) [package="5 mm [THT]"]
  LED13 = RGB LED (com. anode, rbg) [package="5 mm [THT]"]
  LED14 = RGB LED (com. anode, rbg) [package="5 mm [THT]"]
  LED15 = RGB LED (com. anode, rbg) [package="5 mm [THT]"]
  U1 = 74HC595 [package="DIP16 [THT]"]
  R1 = Resistor [tolerance=±5% resistance=1k package=THT]
  R2 = Resistor [tolerance=±5% resistance=1k package=THT]
  R4 = Resistor [tolerance=±5% resistance=1k package=THT]
  R5 = Resistor [tolerance=±5% resistance=220 package=THT]
  R6 = Resistor [tolerance=±5% resistance=220 package=THT]
  R7 = Resistor [tolerance=±5% resistance=220 package=THT]
  R8 = Resistor [tolerance=±5% resistance=220 package=THT]
  R9 = Resistor [tolerance=±5% resistance=220 package=THT]
  R10 = Resistor [tolerance=±5% resistance=220 package=THT]
  R11 = Resistor [tolerance=±5% resistance=220 package=THT]
  R12 = Resistor [tolerance=±5% resistance=220 package=THT]
  R13 = Resistor [tolerance=±5% resistance=220 package=THT]
  R14 = Resistor [tolerance=±5% resistance=220 package=THT]
  R15 = Resistor [tolerance=±5% resistance=220 package=THT]
  R16 = Resistor [tolerance=±5% resistance=220 package=THT]
  U2 = 74HC595 [package="DIP16 [THT]"]
  LED0 = RGB LED (com. anode, rbg) [package="5 mm [THT]"]
  R3 = Resistor [tolerance=±5% resistance=1k package=THT]
  J1 = male pin header, 5 pins [form="♂ (male)"]
  Q1 = PNP-Transistor [part_number=2N4402 package="TO92 [THT]"]
  Q2 = PNP-Transistor [part_number=2N4402 package="TO92 [THT]"]
  Q4 = PNP-Transistor [part_number=2N4402 package="TO92 [THT]"]
  Q3 = PNP-Transistor [part_number=2N4402 package="TO92 [THT]"]
  D1 = Schottky Diode [part_number=BAT43 package="300 mil [THT]"]
  D2 = Schottky Diode [part_number=BAT43 package="300 mil [THT]"]
  D3 = Schottky Diode [part_number=BAT43 package="300 mil [THT]"]
  D4 = Schottky Diode [part_number=BAT43 package="300 mil [THT]"]
  R17 = Resistor [tolerance=±5% resistance=1.5k package=THT]
  R18 = Resistor [tolerance=±5% resistance=1.5k package=THT]
  R19 = Resistor [tolerance=±5% resistance=1.5k package=THT]
  R20 = Resistor [tolerance=±5% resistance=1.5k package=THT]

nets:
  N1: LED1.red_cathode, LED5.red_cathode, LED9.red_cathode, LED13.red_cathode, R8.Pin_1
  N2: LED1.common_anode, LED2.common_anode, LED3.common_anode, LED0.common_anode, Q1.C, D1.anode, R17.Pin_0
  N3: LED1.blue_cathode, LED5.blue_cathode, LED9.blue_cathode, LED13.blue_cathode, R9.Pin_1
  N4: LED1.green_cathode, LED5.green_cathode, LED9.green_cathode, LED13.green_cathode, R10.Pin_1
  N5: LED2.red_cathode, LED6.red_cathode, LED10.red_cathode, LED14.red_cathode, R11.Pin_1
  N6: LED2.blue_cathode, LED6.blue_cathode, LED10.blue_cathode, LED14.blue_cathode, R12.Pin_1
  N7: LED2.green_cathode, LED6.green_cathode, LED10.green_cathode, LED14.green_cathode, R13.Pin_1
  N8: LED3.red_cathode, LED7.red_cathode, LED11.red_cathode, LED15.red_cathode, R14.Pin_1
  N9: LED3.blue_cathode, LED7.blue_cathode, LED11.blue_cathode, LED15.blue_cathode, R15.Pin_1
  N10: LED3.green_cathode, LED7.green_cathode, LED11.green_cathode, LED15.green_cathode, R16.Pin_1
  N11: LED4.red_cathode, LED8.red_cathode, LED12.red_cathode, R5.Pin_1, LED0.red_cathode
  N12: LED4.common_anode, LED5.common_anode, LED6.common_anode, LED7.common_anode, Q2.C, D2.anode, R18.Pin_0
  N13: LED4.blue_cathode, LED8.blue_cathode, LED12.blue_cathode, R6.Pin_1, LED0.blue_cathode
  N14: LED4.green_cathode, LED8.green_cathode, LED12.green_cathode, R7.Pin_1, LED0.green_cathode
  N15: LED8.common_anode, LED9.common_anode, LED10.common_anode, LED11.common_anode, Q3.C, D3.anode, R19.Pin_0
  N16: LED12.common_anode, LED13.common_anode, LED14.common_anode, LED15.common_anode, Q4.C, D4.anode, R20.Pin_0
  N17: U1.Q1, R6.Pin_0
  N18: U1.Q2, R7.Pin_0
  N19: U1.Q3, R8.Pin_0
  N20: U1.Q4, R9.Pin_0
  N21: U1.Q5, R10.Pin_0
  N22: U1.Q6, R11.Pin_0
  N23: U1.Q7, R12.Pin_0
  GND: U1.GND, U1.OE, U2.GND, U2.OE, J1.pin2, R17.Pin_1, R18.Pin_1, R19.Pin_1, R20.Pin_1
  N24: U1.Q7', U2.DS
  VCC: U1.MR, U1.VCC, U2.MR, U2.VCC, J1.pin1, Q1.E, Q2.E, Q4.E, Q3.E
  N25: U1.SH_CP, U2.SH_CP, J1.pin4
  N26: U1.ST_CP, U2.ST_CP, J1.pin5
  N27: U1.DS, J1.pin3
  N28: U1.Q0, R5.Pin_0
  N29: R1.Pin_0, Q1.B, D1.cathode
  N30: R1.Pin_1, U2.Q4
  N31: R2.Pin_0, Q2.B, D2.cathode
  N32: R2.Pin_1, U2.Q5
  N33: R4.Pin_0, Q4.B, D4.cathode
  N34: R4.Pin_1, U2.Q7
  N35: R13.Pin_0, U2.Q0
  N36: R14.Pin_0, U2.Q1
  N37: R15.Pin_0, U2.Q2
  N38: R16.Pin_0, U2.Q3
  N39: U2.Q6, R3.Pin_1
  N40: R3.Pin_0, Q3.B, D3.cathode

notes:
  +5V
  GND
  SER
  CLK
  LATCH
  4x4 RBG LED Matrix
  www.kamprath.net/led-matrix
  (c) 2017 Michael Kamprath
