# Fritzing sketch teensy3.6-5v-logic (saved by Fritzing 0.9.3b)
circuit board: 9.982cm x 2.04501cm
breadboards: 1

parts:
  IC1 = IC, DIP package, 14 pins [chip_label=74HCT125]
  Teensy1 = Teensy 3.6 (Basic)
  J1 = male pin header, 5 pins [form="♂ (male)"]
  C1 = Ceramic Capacitor [capacitance=100nF package="100 mil [THT, multilayer]"]

nets:
  GND: IC1.pin1, IC1.pin4, IC1.pin7, IC1.pin10, Teensy1.GND, Teensy1.GND1, J1.pin2, C1.1
  N1: IC1.pin2, Teensy1.D11
  N2: IC1.pin3, J1.pin3
  N3: IC1.pin5, Teensy1.D13
  N4: IC1.pin6, J1.pin4
  N5: IC1.pin8, J1.pin5
  N6: IC1.pin9, Teensy1.D10
  N7: IC1.pin14, Teensy1.Vin, J1.pin1, C1.0
  N8: Teensy1.3V3, Teensy1.3V3_1

notes:
  5V
  GND
  SER
  CLK
  LATCH
  This jumper connects to the similarly labeled jumper pins on the RGB LED Matrix.

custom parts:
  Teensy 3.6 (Basic): The Teensy is a complete USB-based microcontoller development system, in a very small footprint, capable of implementing many types of projects. All programming is done via the USB port. No special programmer is needed, only a standard micro-USB cable and a PC or Macintosh with a USB port.
